# Fritzing sketch Caso2_2 (saved by Fritzing 0.9.3b)
breadboards: 1

parts:
  Componente3 = Arduino Uno (Rev3)
  Display3 = LCD screen 16x2 IIC [part_number=101290]  # not connected
  LED3 = LED - 5mm [color="Red (633nm)" package="5 mm [THT]"]
  R2 = Resistor [tolerance=±5% resistance=220 package=THT]
  J3 = Piezo Speaker
  Componente4 = Breakout Board for Electret Microphone

nets:
  N1: Componente3.D8, R2.Pin_0
  N2: Componente3.D10_PWM/SS, Componente4.AUD
  GND: Componente3.GND, LED3.cathode, J3.pin1, Componente4.GND
  5V: Componente3.5V, J3.pin2, Componente4.VCC

custom parts:
  LCD screen 16x2 IIC: LCD screen with HD44780 controller enables showing text, symbols, value or anything else that comes from Croduino/Arduino. It is capable of showing 16 symbols in two lines and therefore can be used in many projects that need to send clearly visible and legible output information.. • Color of symbols: White • Backlight: Blue • Dimensions: 80 x 36 x 12 mm • Screen dimensions: 64.5 x 16 mm •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
