# Fritzing sketch Caso_1 (saved by Fritzing 0.9.3b)

parts:
  Componente1 = Arduino Uno (Rev3)
  DHT1 = DHT11 Humitidy and Temperature Sensor (3 pins)
  Display1 = LCD screen 16x2 IIC [part_number=101290]
  R1 = Resistor [tolerance=±5% resistance=220 package=THT]
  LED1 = LED - 5mm [color="Red (633nm)" package="5 mm [THT]"]
  J2 = Piezo Speaker
  Componente2 = pinocc.io protoboard  # not connected

nets:
  N1: Componente1.A4/SDA, Display1.SDA
  N2: Componente1.A5/SCL, Display1.SCL
  N3: Componente1.D8, LED1.anode
  GND: Componente1.GND, DHT1.Gnd, Display1.GND, R1.Pin_0
  N4: Componente1.D2, DHT1.Signal
  5V: Componente1.5V, DHT1.Plus, Display1.VCC, J2.pin2

custom parts:
  DHT11 Humitidy and Temperature Sensor (3 pins): DHT11 Humidity and Temperature Sensor (3 pins).
  LCD screen 16x2 IIC: LCD screen with HD44780 controller enables showing text, symbols, value or anything else that comes from Croduino/Arduino. It is capable of showing 16 symbols in two lines and therefore can be used in many projects that need to send clearly visible and legible output information.. • Color of symbols: White • Backlight: Blue • Dimensions: 80 x 36 x 12 mm • Screen dimensions: 64.5 x 16 mm •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
