# Fritzing sketch Caso_2 (saved by Fritzing 0.9.3b)

parts:
  Componente1 = Arduino Uno (Rev3)
  Display1 = LCD screen 16x2 IIC [part_number=101290]
  R1 = Resistor [tolerance=±5% resistance=220 package=THT]
  LED1 = LED - 5mm [color="Yellow (595nm)" package="5 mm [THT]"]
  J2 = Piezo Speaker
  Componente3 = Breakout Board for Electret Microphone

nets:
  N1: Componente1.A4/SDA, Display1.SDA
  N2: Componente1.A5/SCL, Display1.SCL
  N3: Componente1.D8, LED1.anode
  N4: Componente1.D9_PWM, J2.pin2
  N5: Componente1.D10_PWM/SS, Componente3.AUD
  GND: Componente1.GND, Display1.GND, R1.Pin_0, J2.pin1, Componente3.GND
  VCC: Componente1.5V, Display1.VCC, Componente3.VCC

custom parts:
  LCD screen 16x2 IIC: LCD screen with HD44780 controller enables showing text, symbols, value or anything else that comes from Croduino/Arduino. It is capable of showing 16 symbols in two lines and therefore can be used in many projects that need to send clearly visible and legible output information.. • Color of symbols: White • Backlight: Blue • Dimensions: 80 x 36 x 12 mm • Screen dimensions: 64.5 x 16 mm •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
